// Logisim project ROMandCommandCounter.circ as structural Verilog: 1 circuit, main circuit main
module main (
);

  wire and_1_out, and_2_out, and_3_out, and_4_out, clock_1_out, controlled_buffer_1_out,
       controlled_buffer_2_out, controlled_buffer_4_out, controlled_buffer_5_out, controlled_buffer_6_out,
       controlled_buffer_7_out, controlled_buffer_8_out, controlled_buffer_10_out, controlled_buffer_12_out,
       controlled_buffer_13_out, controlled_buffer_14_out, controlled_buffer_16_out,
       controlled_buffer_18_out, controlled_buffer_19_out, controlled_buffer_21_out,
       controlled_buffer_23_out, controlled_buffer_24_out, controlled_buffer_26_out,
       controlled_buffer_28_out, controlled_buffer_30_out, controlled_buffer_32_out,
       controlled_buffer_34_out, controlled_buffer_36_out, controlled_buffer_38_out,
       controlled_buffer_40_out, controlled_buffer_42_out, d_ff_1_q, d_ff_2_q, d_ff_2_qn, d_ff_3_q, d_ff_4_q,
       d_ff_4_qn, d_ff_5_qn, d_ff_6_qn, d_ff_7_q, d_ff_8_q, d_ff_9_q, d_ff_10_q, d_ff_11_qn, d_ff_12_q,
       d_ff_13_q, d_ff_14_qn, d_ff_15_q, d_ff_16_qn, d_ff_17_q, d_ff_18_qn, d_ff_19_qn, d_ff_20_qn,
       d_ff_21_qn, d_ff_22_qn, decoder_1_out0, decoder_1_out1, nand_1_out, nor_1_out, nor_2_out, nor_3_out,
       not_1_out, not_2_out, pull_resistor_1_node;
  wire [1:0] d_ff_5_q;
  wire [7:0] d_ff_11_q, rom_1_data;

  and and_1 (and_1_out, clock_1_out, decoder_1_out0);
  D_Flip_Flop #(.trigger("falling")) d_ff_1 (.D(nor_3_out), .clk(and_1_out), .Q(d_ff_1_q));  // open: Qn, preset, reset
  D_Flip_Flop #(.trigger("falling")) d_ff_2 (
    .D(d_ff_2_qn), .clk(controlled_buffer_1_out), .Q(d_ff_2_q), .Qn(d_ff_2_qn), .reset(and_2_out));  // open: preset
  assign controlled_buffer_1_out = d_ff_2_qn ? and_1_out : 1'bz;  // Controlled_Buffer controlled_buffer_1
  assign controlled_buffer_2_out = d_ff_4_qn ? decoder_1_out0 : 1'bz;  // Controlled_Buffer controlled_buffer_2
  and and_2 (and_2_out, nor_3_out, not_1_out);
  not not_1 (not_1_out, d_ff_1_q);
  D_Flip_Flop d_ff_3 (.D(nor_2_out), .clk(decoder_1_out1), .Q(d_ff_3_q), .reset(not_2_out));  // open: Qn, preset
  not not_2 (not_2_out, nor_2_out);
  D_Flip_Flop #(.trigger("falling")) d_ff_4 (
    .D(d_ff_4_qn), .clk(controlled_buffer_2_out), .Q(d_ff_4_q), .Qn(d_ff_4_qn), .reset(d_ff_3_q));  // open: preset
  D_Flip_Flop #(.trigger("falling")) d_ff_5 (
    .D(d_ff_5_qn), .clk(clock_1_out), .Q(d_ff_5_q[0]), .Qn(d_ff_5_qn));  // open: preset, reset
  Clock clock_1 (.out(clock_1_out));
  nor nor_1 (nor_1_out, and_2_out, nor_2_out);
  nor nor_2 (nor_2_out, nor_1_out, d_ff_2_q);
  Button button_1 ();  // open: out
  Pull_Resistor pull_resistor_1 (.node(pull_resistor_1_node));
  assign pull_resistor_1_node = d_ff_4_q ? decoder_1_out0 : 1'bz;  // Controlled_Buffer controlled_buffer_3
  Decoder #(.select(2)) decoder_1 (
    .out0(decoder_1_out0), .out1(decoder_1_out1), .sel(d_ff_5_q));  // open: out2, out3, en
  D_Flip_Flop #(.trigger("falling")) d_ff_6 (
    .D(d_ff_6_qn), .clk(d_ff_5_q[0]), .Q(d_ff_5_q[1]), .Qn(d_ff_6_qn));  // open: preset, reset
  nand nand_1 (nand_1_out, 1'b1, d_ff_3_q);
  D_Flip_Flop d_ff_7 (.D(controlled_buffer_4_out), .clk(and_3_out), .Q(d_ff_7_q));  // open: Qn, preset, reset
  assign controlled_buffer_4_out = nand_1_out ? rom_1_data[0] : 1'bz;  // Controlled_Buffer controlled_buffer_4
  and and_3 (and_3_out, clock_1_out, decoder_1_out1);
  and and_4 (and_4_out, pull_resistor_1_node, clock_1_out);
  assign controlled_buffer_5_out = nand_1_out ? rom_1_data[1] : 1'bz;  // Controlled_Buffer controlled_buffer_5
  Pull_Resistor pull_resistor_2 (.node(d_ff_3_q));
  D_Flip_Flop d_ff_8 (.D(controlled_buffer_5_out), .clk(and_3_out), .Q(d_ff_8_q));  // open: Qn, preset, reset
  D_Flip_Flop d_ff_9 (.D(controlled_buffer_6_out), .clk(and_3_out), .Q(d_ff_9_q));  // open: Qn, preset, reset
  assign controlled_buffer_6_out = nand_1_out ? rom_1_data[2] : 1'bz;  // Controlled_Buffer controlled_buffer_6
  ROM rom_1 (.addr(d_ff_11_q), .data(rom_1_data));
  nor nor_3 (nor_3_out, d_ff_7_q, d_ff_8_q, d_ff_9_q, d_ff_10_q, d_ff_12_q, d_ff_13_q, d_ff_15_q, d_ff_17_q);
  assign controlled_buffer_7_out = nand_1_out ? rom_1_data[3] : 1'bz;  // Controlled_Buffer controlled_buffer_7
  assign controlled_buffer_8_out = d_ff_3_q ? rom_1_data[0] : 1'bz;  // Controlled_Buffer controlled_buffer_8
  assign controlled_buffer_8_out = nand_1_out ? d_ff_11_qn : 1'bz;  // Controlled_Buffer controlled_buffer_9
  assign controlled_buffer_10_out = nand_1_out ? and_4_out : 1'bz;  // Controlled_Buffer controlled_buffer_10
  assign controlled_buffer_10_out = d_ff_3_q ? decoder_1_out1 : 1'bz;  // Controlled_Buffer controlled_buffer_11
  D_Flip_Flop d_ff_10 (.D(controlled_buffer_7_out), .clk(and_3_out), .Q(d_ff_10_q));  // open: Qn, preset, reset
  assign controlled_buffer_12_out = nand_1_out ? rom_1_data[4] : 1'bz;  // Controlled_Buffer controlled_buffer_12
  D_Flip_Flop #(.trigger("falling")) d_ff_11 (
    .D(controlled_buffer_8_out), .clk(controlled_buffer_10_out), .Q(d_ff_11_q[0]), .Qn(d_ff_11_qn));  // open: preset, reset
  D_Flip_Flop d_ff_12 (.D(controlled_buffer_12_out), .clk(and_3_out), .Q(d_ff_12_q));  // open: Qn, preset, reset
  assign controlled_buffer_13_out = nand_1_out ? d_ff_14_qn : 1'bz;  // Controlled_Buffer controlled_buffer_13
  assign controlled_buffer_14_out = nand_1_out ? d_ff_11_q[0] : 1'bz;  // Controlled_Buffer controlled_buffer_14
  assign controlled_buffer_14_out = d_ff_3_q ? controlled_buffer_10_out : 1'bz;  // Controlled_Buffer controlled_buffer_15
  D_Flip_Flop d_ff_13 (.D(controlled_buffer_16_out), .clk(and_3_out), .Q(d_ff_13_q));  // open: Qn, preset, reset
  assign controlled_buffer_16_out = nand_1_out ? rom_1_data[5] : 1'bz;  // Controlled_Buffer controlled_buffer_16
  assign controlled_buffer_13_out = d_ff_3_q ? rom_1_data[1] : 1'bz;  // Controlled_Buffer controlled_buffer_17
  D_Flip_Flop #(.trigger("falling")) d_ff_14 (
    .D(controlled_buffer_13_out), .clk(controlled_buffer_14_out), .Q(d_ff_11_q[1]), .Qn(d_ff_14_qn));  // open: preset, reset
  assign controlled_buffer_18_out = nand_1_out ? rom_1_data[6] : 1'bz;  // Controlled_Buffer controlled_buffer_18
  assign controlled_buffer_19_out = nand_1_out ? d_ff_16_qn : 1'bz;  // Controlled_Buffer controlled_buffer_19
  D_Flip_Flop d_ff_15 (.D(controlled_buffer_18_out), .clk(and_3_out), .Q(d_ff_15_q));  // open: Qn, preset, reset
  assign controlled_buffer_19_out = d_ff_3_q ? rom_1_data[2] : 1'bz;  // Controlled_Buffer controlled_buffer_20
  D_Flip_Flop #(.trigger("falling")) d_ff_16 (
    .D(controlled_buffer_19_out), .clk(controlled_buffer_21_out), .Q(d_ff_11_q[2]), .Qn(d_ff_16_qn));  // open: preset, reset
  assign controlled_buffer_21_out = nand_1_out ? d_ff_11_q[1] : 1'bz;  // Controlled_Buffer controlled_buffer_21
  assign controlled_buffer_21_out = d_ff_3_q ? controlled_buffer_14_out : 1'bz;  // Controlled_Buffer controlled_buffer_22
  D_Flip_Flop d_ff_17 (.D(controlled_buffer_23_out), .clk(and_3_out), .Q(d_ff_17_q));  // open: Qn, preset, reset
  assign controlled_buffer_23_out = nand_1_out ? rom_1_data[7] : 1'bz;  // Controlled_Buffer controlled_buffer_23
  assign controlled_buffer_24_out = d_ff_3_q ? rom_1_data[3] : 1'bz;  // Controlled_Buffer controlled_buffer_24
  assign controlled_buffer_24_out = nand_1_out ? d_ff_18_qn : 1'bz;  // Controlled_Buffer controlled_buffer_25
  assign controlled_buffer_26_out = nand_1_out ? d_ff_11_q[2] : 1'bz;  // Controlled_Buffer controlled_buffer_26
  assign controlled_buffer_26_out = d_ff_3_q ? controlled_buffer_21_out : 1'bz;  // Controlled_Buffer controlled_buffer_27
  D_Flip_Flop #(.trigger("falling")) d_ff_18 (
    .D(controlled_buffer_24_out), .clk(controlled_buffer_26_out), .Q(d_ff_11_q[3]), .Qn(d_ff_18_qn));  // open: preset, reset
  assign controlled_buffer_28_out = nand_1_out ? d_ff_19_qn : 1'bz;  // Controlled_Buffer controlled_buffer_28
  assign controlled_buffer_28_out = d_ff_3_q ? rom_1_data[4] : 1'bz;  // Controlled_Buffer controlled_buffer_29
  D_Flip_Flop #(.trigger("falling")) d_ff_19 (
    .D(controlled_buffer_28_out), .clk(controlled_buffer_30_out), .Q(d_ff_11_q[4]), .Qn(d_ff_19_qn));  // open: preset, reset
  assign controlled_buffer_30_out = nand_1_out ? d_ff_11_q[3] : 1'bz;  // Controlled_Buffer controlled_buffer_30
  assign controlled_buffer_30_out = d_ff_3_q ? controlled_buffer_26_out : 1'bz;  // Controlled_Buffer controlled_buffer_31
  assign controlled_buffer_32_out = d_ff_3_q ? rom_1_data[5] : 1'bz;  // Controlled_Buffer controlled_buffer_32
  assign controlled_buffer_32_out = nand_1_out ? d_ff_20_qn : 1'bz;  // Controlled_Buffer controlled_buffer_33
  assign controlled_buffer_34_out = nand_1_out ? d_ff_11_q[4] : 1'bz;  // Controlled_Buffer controlled_buffer_34
  assign controlled_buffer_34_out = d_ff_3_q ? controlled_buffer_30_out : 1'bz;  // Controlled_Buffer controlled_buffer_35
  D_Flip_Flop #(.trigger("falling")) d_ff_20 (
    .D(controlled_buffer_32_out), .clk(controlled_buffer_34_out), .Q(d_ff_11_q[5]), .Qn(d_ff_20_qn));  // open: preset, reset
  assign controlled_buffer_36_out = d_ff_3_q ? rom_1_data[6] : 1'bz;  // Controlled_Buffer controlled_buffer_36
  assign controlled_buffer_36_out = nand_1_out ? d_ff_21_qn : 1'bz;  // Controlled_Buffer controlled_buffer_37
  assign controlled_buffer_38_out = nand_1_out ? d_ff_11_q[5] : 1'bz;  // Controlled_Buffer controlled_buffer_38
  assign controlled_buffer_38_out = d_ff_3_q ? controlled_buffer_34_out : 1'bz;  // Controlled_Buffer controlled_buffer_39
  D_Flip_Flop #(.trigger("falling")) d_ff_21 (
    .D(controlled_buffer_36_out), .clk(controlled_buffer_38_out), .Q(d_ff_11_q[6]), .Qn(d_ff_21_qn));  // open: preset, reset
  assign controlled_buffer_40_out = nand_1_out ? d_ff_22_qn : 1'bz;  // Controlled_Buffer controlled_buffer_40
  assign controlled_buffer_40_out = d_ff_3_q ? rom_1_data[7] : 1'bz;  // Controlled_Buffer controlled_buffer_41
  D_Flip_Flop #(.trigger("falling")) d_ff_22 (
    .D(controlled_buffer_40_out), .clk(controlled_buffer_42_out), .Q(d_ff_11_q[7]), .Qn(d_ff_22_qn));  // open: preset, reset
  assign controlled_buffer_42_out = nand_1_out ? d_ff_11_q[6] : 1'bz;  // Controlled_Buffer controlled_buffer_42
  assign controlled_buffer_42_out = d_ff_3_q ? controlled_buffer_38_out : 1'bz;  // Controlled_Buffer controlled_buffer_43

  // Notes on the sheet:
  //   contents of rom_1 (hex, n*v repeats v):
  //   11 22 33 44 55 66 77 88 99 0 10 5*0 10*ff
endmodule
